# Fritzing sketch Detector (saved by Fritzing 0.8.7b)
circuit board: 5.50591cm x 2.56542cm
breadboards: 1

parts:
  LED1 = LEDs [package=led10mm]
  Q1 = NPN-Transistor [package="TO92 [THT]"]
  Q2 = NPN-Transistor [package="TO92 [THT]"]
  LaserDiode = LEDs [package=led10mm]
  Q3 = NPN-Transistor [package="TO92 [THT]"]
  R1 = Resistor [tolerance=±5% resistance=220 package=THT]
  R2 = Resistor [tolerance=±5% resistance=220 package=THT]
  V_Do_G_Di = female pin header, 4 pins [form="♀ (female)"]

nets:
  N1: LED1.A, Q1.B
  N2: LED1.C, Q1.E, Q2.B
  N3: Q1.C, R2.Pin_0, V_Do_G_Di.pin1
  N4: Q2.E, Q3.E, V_Do_G_Di.pin3
  N5: Q2.C, V_Do_G_Di.pin2
  N6: LaserDiode.A, R2.Pin_1
  N7: LaserDiode.C, Q3.C
  N8: Q3.B, R1.Pin_1
  N9: R1.Pin_0, V_Do_G_Di.pin4
